# Fritzing sketch Turn Signals v2.1 (saved by Fritzing 0.7.10b)

parts:
  U1 = Voltage Regulator - 5V [package="TO220 [THT]"]
  C2 = Electrolytic Capacitor [package=THT]
  R10 = Resistor [resistance=22k tolerance=±5% package=THT]
  R11 = Resistor [resistance=4.7k tolerance=±5% package=THT]
  D5 = Rectifier Diode [package=THT]
  D6 = Rectifier Diode [package=THT]
  R12 = Resistor [resistance=10k tolerance=±5% package=THT]
  C3 = Ceramic Capacitor [package=THT]
  PR = female pin header, 1 pin [form="♂ (male)"]
  D7 = Rectifier Diode [package=THT]
  D8 = Rectifier Diode [package=THT]
  R14 = Resistor [resistance=22k tolerance=±5% package=THT]
  R15 = Resistor [resistance=4.7k tolerance=±5% package=THT]
  PR_2 = female pin header, 1 pin [form="♂ (male)"]
  J19 = screw terminal, 3 pins
  IC1 = PICAXE-14M [package=THT]
  IC2 = ULN2803A [package=THT]
  R13 = Resistor [tolerance=±5% resistance=22k package=THT]
  Serial = male pin header, 3 pins [form="♂ (male)"]
  LEDs = male pin header, 9 pins [form="♂ (male)"]

nets:
  N1: U1.input_voltage, C2.+, D6.cathode, C3.pin_0, D8.cathode, LEDs.pin1
  GND: U1.GND, C2.-, R10.Pin_1, R12.Pin_1, C3.pin_1, PR.pin1, J19.pin1, IC1.0V, IC2.0V, R13.Pin_1, Serial.pin1
  N2: U1.output_voltage, D5.cathode, D7.cathode, IC1.+V
  N3: R10.Pin_0, R11.Pin_0, D7.anode, IC1.In_3_/_Infrain
  N4: R11.Pin_1, D6.anode, J19.pin3
  N5: D5.anode, R15.Pin_0, IC1.In_4_/_ADC_4, R13.Pin_0
  N6: R12.Pin_0, R14.Pin_1, Serial.pin2
  N7: D8.anode, R15.Pin_1, PR_2.pin1, J19.pin2
  N8: R14.Pin_0, IC1.Serial_In
  N9: IC1.In_1, IC2.In_8
  N10: IC1.In_0_/_ADC_0, IC2.In_7
  N11: IC1.Out_5, IC2.In_6
  N12: IC1.Out_4, IC2.In_5
  N13: IC1.Out_3, IC2.In_4
  N14: IC1.Out_2, IC2.In_3
  N15: IC1.Out_1, IC2.In_2
  N16: IC1.Serial_Out_/_Out_0_/_Infraout, IC2.In_1, Serial.pin3
  N17: IC2.Out_8, LEDs.pin9
  N18: IC2.Out_7, LEDs.pin8
  N19: IC2.Out_6, LEDs.pin7
  N20: IC2.Out_5, LEDs.pin6
  N21: IC2.Out_4, LEDs.pin5
  N22: IC2.Out_3, LEDs.pin4
  N23: IC2.Out_2, LEDs.pin3
  N24: IC2.Out_1, LEDs.pin2

notes:
  Animated Turn
  Signals   V2.1
  Gnd
  Bl
  Li
